# Fritzing sketch Colorsorter Microcontroller (saved by Fritzing 0.9.6b)
perfboards: 1

parts:
  Nano = Arduino Nano (Rev3.0)
  LightSensor = Adafruit APDS-9960 [part_number="Adafruit #3595"]
  Selector = Dagu DGServo 9g (End View) [part_number=RS001B]
  Ejector = Dagu DGServo 9g (End View) [part_number=RS001B]
  R1 = Resistor [tolerance=±5% power=0.25 resistance=22 package=THT]
  LED2 = LED - 3mm [color="White (4500K)" current=0.030 package="3 mm [THT]"]  # not connected
  LED1 = LED - 3mm [color="White (4500K)" current=0.030 package="3 mm [THT]"]  # not connected
  R2 = Resistor [tolerance=±5% power=0.25 resistance=22 package=THT]
  R3 = Trimmer Potentiometer [maximum_resistance=10kΩ package=THT]  # not connected

nets:
  N1: Nano.D5, Selector.pulse
  N2: Nano.D6, Ejector.pulse
  N3: Nano.D9, R1.Pin_1, R2.Pin_1
  GND: Nano.GND, LightSensor.GND, Selector.gnd, Ejector.gnd
  VCC: Nano.5V, Selector.vcc, Ejector.vcc
  N4: Nano.A5, LightSensor.SCL
  N5: Nano.A4, LightSensor.SDA
  3V3: Nano.3V3, LightSensor.3.3V

custom parts:
  Adafruit APDS-9960: The APDS9960 from Avago Technologies has an integrated IR LED and driver, along with four directional photodiodes that sense reflected IR energy from the LED. It's proximity detection feature allows it to measure the distance an object is from the front of the sensor (up to a few centimeters) with 8 bit resolution. Since there are four IR sensors, you can measure the changes in light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
